// Logisim project extra.circ as structural Verilog: 3 circuits, main circuit main
module main (
  input  CLK,
  input  [3:0] X,
  output [3:0] Y
);

  flip flip_1 (.in_2(X[0]), .in_1(CLK), .Q(Y[0]));
  flip flip_2 (.in_2(X[1]), .in_1(CLK), .Q(Y[1]));
  flip flip_3 (.in_2(X[2]), .in_1(CLK), .Q(Y[2]));
  flip flip_4 (.in_2(X[3]), .in_1(CLK), .Q(Y[3]));
endmodule

module dlatch (
  input  CLK,
  input  D,
  output Q,
  output Q_prime
);

  wire and_1_out, and_2_out, not_1_out;

  not not_1 (not_1_out, D);
  and and_1 (and_1_out, CLK, not_1_out);
  and and_2 (and_2_out, CLK, D);
  nor nor_1 (Q, and_1_out, Q_prime);
  nor nor_2 (Q_prime, Q, and_2_out);
endmodule

module flip (
  input  in_1,
  input  in_2,
  output Q
);

  wire dlatch_1_q, not_1_out;

  not not_1 (not_1_out, in_1);
  dlatch dlatch_1 (.CLK(not_1_out), .D(in_2), .Q(dlatch_1_q));  // open: Q_prime
  dlatch dlatch_2 (.CLK(in_1), .D(dlatch_1_q), .Q(Q));  // open: Q_prime
endmodule
