// Logisim project task3.circ as structural Verilog: 1 circuit, main circuit main
module main (
  input  Cin,
  input  [3:0] A,
  input  [3:0] S,
  input  [3:0] B,
  input  Cin_2,
  input  [3:0] A_2,
  input  [3:0] S_2,
  input  [3:0] B_2,
  output Cout,
  output Cout_2
);

  wire adder_2_cout, adder_3_cout, adder_4_cout;

  Adder #(.width(4)) adder_1 (.a(A), .b(B), .out(S), .cin(Cin), .cout(Cout));
  Adder #(.width(1)) adder_2 (.a(A_2[0]), .b(B_2[0]), .out(S_2[0]), .cin(Cin_2), .cout(adder_2_cout));
  Adder #(.width(1)) adder_3 (.a(A_2[1]), .b(B_2[1]), .out(S_2[1]), .cin(adder_2_cout), .cout(adder_3_cout));
  Adder #(.width(1)) adder_4 (.a(A_2[2]), .b(B_2[2]), .out(S_2[2]), .cin(adder_3_cout), .cout(adder_4_cout));
  Adder #(.width(1)) adder_5 (.a(A_2[3]), .b(B_2[3]), .out(S_2[3]), .cin(adder_4_cout), .cout(Cout_2));
endmodule
