// Logisim project task4.circ as structural Verilog: 1 circuit, main circuit main
module main (
  input  D,
  input  CLK,
  input  R,
  input  S,
  output Q_prime,
  output Q,
  output Q_2,
  output Q_prime_2
);

  wire and_1_out, and_2_out, not_1_out;

  not not_1 (not_1_out, D);
  and and_1 (and_1_out, D, CLK);
  and and_2 (and_2_out, not_1_out, CLK);
  nor nor_1 (Q_prime, and_1_out, Q);
  nor nor_2 (Q, Q_prime, and_2_out);
  nor nor_3 (Q_2, R, Q_prime_2);
  nor nor_4 (Q_prime_2, Q_2, S);
endmodule
