// Logisim project task5.circ as structural Verilog: 2 circuits, main circuit main
module main (
  input  in_1,
  input  in_2,
  output out_3
);

  wire not_1_out;

  not not_1 (not_1_out, in_1);
  Dlatch dlatch_1 (.CLK(not_1_out), .D(in_2), .Q(in_1), .Q_prime(in_1));
  Dlatch dlatch_2 (.CLK(in_1), .D(in_1), .Q(out_3));  // open: Q_prime
endmodule

module Dlatch (
  input  CLK,
  input  D,
  output Q,
  output Q_prime
);

  wire and_1_out, and_2_out, not_1_out;

  not not_1 (not_1_out, D);
  and and_1 (and_1_out, CLK, not_1_out);
  and and_2 (and_2_out, CLK, D);
  nor nor_1 (Q, and_1_out, Q_prime);
  nor nor_2 (Q_prime, Q, and_2_out);
endmodule
